# Fritzing sketch drone schematic (saved by Fritzing 0.9.3b)

parts:
  Part1 = Arduino Mega 2560 (Rev3)
  Part2 = NRF24L01+ Breakout Board
  J1 = female pin header, 3 pins [form="♀ (female)"]
  J2 = female pin header, 3 pins [form="♀ (female)"]
  J3 = female pin header, 3 pins [form="♀ (female)"]
  J4 = female pin header, 3 pins [form="♀ (female)"]
  J5 = female pin header, 3 pins [form="♀ (female)"]
  J6 = female pin header, 3 pins [form="♀ (female)"]
  J7 = female pin header, 3 pins [form="♀ (female)"]
  J8 = female pin header, 3 pins [form="♀ (female)"]
  J9 = female pin header, 3 pins [form="♀ (female)"]

nets:
  GND: Part1.GND, Part2.GND
  N1: Part1.D13_PWM, Part2.SCK
  N2: Part1.D12_PWM, Part2.MISO
  N3: Part1.D11_PWM, Part2.MOSI
  N4: Part1.D10_PWM, Part2.CS
  N5: Part1.D9_PWM, Part2.CE
  5V: Part1.5V, Part2.VCC
  N6: Part1.D2_PWM, Part2.IRQ
  N7: Part1.D3_PWM, J1.pin1
  N8: Part1.D4_PWM, J2.pin1
  N9: Part1.D5_PWM, J3.pin1
  N10: Part1.D6_PWM, J4.pin1
  N11: Part1.D7_PWM, J5.pin1
  N12: Part1.D22, J6.pin1
  N13: Part1.D24, J7.pin1
  N14: Part1.D26, J8.pin1
  N15: Part1.D28, J9.pin1

notes:
  AIL
  ELE
  THR
  RUD
  CONNECT AUX 1 DIRECTLY TO FLIGHT CONTROLLER FOR ARMING,
  AUX
  RX
  ail
  ele
  thr
