# Fritzing sketch wearable schematic (saved by Fritzing 0.9.3b)

parts:
  Part1 = NRF24L01+ Breakout Board
  Arduino1 = Arduino Mini (Rev5)
  Part2 = InvenSense MPU6050

nets:
  GND: Part1.GND, Arduino1.GND, Part2.GND
  VCC: Part1.VCC, Arduino1.5V, Part2.VCC
  N1: Part1.CE, Arduino1.D9_PWM
  N2: Part1.CS, Arduino1.D10_PWM
  N3: Part1.SCK, Arduino1.D13
  N4: Part1.MOSI, Arduino1.D11_PWM
  N5: Part1.MISO, Arduino1.D12
  N6: Part1.IRQ, Arduino1.D2
  N7: Arduino1.D4, Part2.SCL
  N8: Arduino1.D5_PWM, Part2.SDA
